# Fritzing sketch led (saved by Fritzing 0.9.3b)
breadboards: 1

parts:
  Componente1 = Arduino Uno (Rev3)
  S1 = Pushbutton [package=THT]
  R1 = Resistor [tolerance=±5% resistance=220 package=THT]
  LED1 = LED - 5mm [color="Red (633nm)" package="5 mm [THT]"]
  R2 = Resistor [tolerance=±5% resistance=220 package=THT]

nets:
  N1: Componente1.D9_PWM, LED1.anode
  N2: Componente1.D7, S1.leg0, R1.Pin_0
  N3: Componente1.5V, R1.Pin_1
  N4: Componente1.GND, S1.leg1, R2.Pin_1
  N5: LED1.cathode, R2.Pin_0
