# Fritzing sketch Dulceria (saved by Fritzing 0.9.3b)
breadboards: 1

parts:
  Componente2 = Arduino Mega 2560 (Rev3)
  Q1 = PHOTOTRANSISTOR REFLECTIVE OBJECT SENSOR [package=qrb1114-side]
  R1 = Resistor [tolerance=±5% resistance=220 package=THT]
  R2 = Resistor [tolerance=±5% resistance=220 package=THT]
  LED1 = LED - 5mm [color="Red (633nm)" package="5 mm [THT]"]  # not connected
  LED2 = LED - 5mm [color="Red (633nm)" package="5 mm [THT]"]  # not connected
  LED3 = LED - 5mm [color="Red (633nm)" package="5 mm [THT]"]  # not connected
  LED4 = LED - 5mm [color="Red (633nm)" package="5 mm [THT]"]  # not connected
  R3 = Resistor [tolerance=±5% resistance=220 package=THT]
  R4 = Resistor [tolerance=±5% resistance=220 package=THT]
  R5 = Resistor [tolerance=±5% resistance=220 package=THT]
  R6 = Resistor [tolerance=±5% resistance=220 package=THT]
  S1 = Pushbutton [package="[THT]"]
  S2 = Pushbutton [package="[THT]"]
  S3 = Pushbutton [package="[THT]"]
  S4 = Pushbutton [package="[THT]"]
  R7 = Resistor [tolerance=±5% resistance=220 package=THT]
  R8 = Resistor [tolerance=±5% resistance=220 package=THT]
  R9 = Resistor [tolerance=±5% resistance=220 package=THT]
  R10 = Resistor [tolerance=±5% resistance=220 package=THT]

nets:
  N1: Componente2.A8, R2.Pin_0
  N2: Componente2.D21/SCL, S1.Pin_1, S1.Pin_2, R7.Pin_0
  N3: Componente2.D20/SDA, S2.Pin_1, R8.Pin_0
  N4: Componente2.D11_PWM, R6.Pin_0
  N5: Componente2.D10_PWM, R5.Pin_0
  N6: Componente2.D9_PWM, R4.Pin_0
  N7: Componente2.D8_PWM, R3.Pin_1
  N8: Componente2.5V, Q1.C, Q1.E, R1.Pin_1, R7.Pin_1, R8.Pin_1, R9.Pin_1, R10.Pin_1
  N9: Componente2.GND, Q1.A, Q1.K, R2.Pin_1, S1.Pin_3, S1.Pin_4, S2.Pin_3, S2.Pin_4, S3.Pin_3, S3.Pin_4, S4.Pin_3, S4.Pin_4
  N10: Componente2.D2_PWM, S4.Pin_1, R10.Pin_0
  N11: Componente2.D3_PWM, S3.Pin_1, R9.Pin_0
