# Fritzing sketch ejercicio2 (saved by Fritzing 0.9.3b)
breadboards: 1

parts:
  Componente1 = Arduino Uno (Rev3)
  J1 = Piezo Speaker
  LED1 = LED - 5mm [color="Red (633nm)" package="5 mm [THT]"]
  R1 = Resistor [tolerance=±5% resistance=220 package=THT]
  R2 = Resistor [tolerance=±5% resistance=220 package=THT]
  LED2 = LED - 5mm [color="Red (633nm)" package="5 mm [THT]"]
  S1 = Pushbutton [package="[THT]"]
  S2 = Pushbutton [package="[THT]"]

nets:
  N1: Componente1.D8, R1.Pin_1
  N2: Componente1.GND, J1.pin1, LED1.cathode, LED2.cathode, S1.Pin_3, S1.Pin_4, S2.Pin_3, S2.Pin_4
  N3: Componente1.D5_PWM, S1.Pin_1, S1.Pin_2
  N4: Componente1.D6_PWM, S2.Pin_1, S2.Pin_2
  N5: Componente1.D7, R2.Pin_1
  N6: LED1.anode, R1.Pin_0
  N7: R2.Pin_0, LED2.anode
